# Fritzing sketch MP3_Serial (saved by Fritzing 0.9.6b)
breadboards: 1

parts:
  Part1 = Franzininho WiFi
  DFRobot_DFPlayer_Mini1 = DFRobot DFPlayer Mini [part_number=DFR0299]
  SPKR1 = Loudspeaker

nets:
  5V: Part1.5V, DFRobot_DFPlayer_Mini1.VCC
  N1: Part1.GND#22, DFRobot_DFPlayer_Mini1.GND-1, DFRobot_DFPlayer_Mini1.GND-2
  N2: Part1.42, DFRobot_DFPlayer_Mini1.BUSY
  N3: Part1.43, DFRobot_DFPlayer_Mini1.RX
  N4: DFRobot_DFPlayer_Mini1.SPK_1, SPKR1.pin2
  N5: DFRobot_DFPlayer_Mini1.SPK_2, SPKR1.pin1

custom parts:
  Franzininho WiFi: Placa de desenvolvimento ESP32-S2
