# Fritzing sketch RFID (saved by Fritzing 0.9.6b)
breadboards: 1

parts:
  Part1 = Franzininho WiFi
  R1 = Resistor [tolerance=±5% power=0.25 resistance=220 package=THT]
  R2 = Resistor [tolerance=±5% power=0.25 resistance=220 package=THT]
  R3 = Resistor [tolerance=±5% power=0.25 resistance=220 package=THT]
  R4 = Resistor [tolerance=±5% power=0.25 resistance=220 package=THT]
  R5 = Resistor [tolerance=±5% power=0.25 resistance=220 package=THT]
  R6 = Resistor [tolerance=±5% power=0.25 resistance=220 package=THT]
  R7 = Resistor [tolerance=±5% power=0.25 resistance=220 package=THT]
  R8 = Resistor [tolerance=±5% power=0.25 resistance=220 package=THT]
  R9 = Resistor [tolerance=±5% power=0.25 resistance=220 package=THT]
  R10 = Resistor [tolerance=±5% power=0.25 resistance=220 package=THT]
  D1 = LED_BARGRAPH_10 [package=led_bargaph_10]
  RDM1 = RDM6300

nets:
  N1: Part1.1, R1.Pin_0
  N2: Part1.2, R2.Pin_0
  N3: Part1.3, R3.Pin_0
  N4: Part1.4, R4.Pin_0
  N5: Part1.5, R5.Pin_0
  N6: Part1.6, R6.Pin_0
  N7: Part1.7, R7.Pin_0
  N8: Part1.10, R8.Pin_0
  N9: Part1.11, R9.Pin_0
  N10: Part1.12, R10.Pin_0
  5V: Part1.5V, RDM1.5V
  N11: Part1.GND#22, D1.J_C, D1.I_C, D1.H_C, D1.F_C, D1.E_C, D1.D_C, D1.C_C, D1.B_C, RDM1.GND
  N12: Part1.44, RDM1.Tx
  N13: R1.Pin_1, D1.J_A
  N14: R2.Pin_1, D1.I_A
  N15: R3.Pin_1, D1.H_A
  N16: R4.Pin_1, D1.G_A
  N17: R5.Pin_1, D1.F_A
  N18: R6.Pin_1, D1.E_A
  N19: R7.Pin_1, D1.D_A
  N20: R8.Pin_1, D1.C_A
  N21: R9.Pin_1, D1.B_A
  N22: R10.Pin_1, D1.A_A

custom parts:
  Franzininho WiFi: Placa de desenvolvimento ESP32-S2
